# Fritzing sketch RASPmini (saved by Fritzing 0.9.3b)
perfboards: 1

parts:
  R2 = Resistor [tolerance=±5% resistance=33k package=THT]
  R1 = Resistor [tolerance=±5% resistance=18k package=THT]

nets:
  N1: R2.Pin_0, R1.Pin_0

notes:
  5v
  3.3v
  SDA
  SCL
  EN
  GND
  3.3v GND SCK MOSI CS MISO GND
  3.3v GND SCK MOSI MISO CS GND
